# Fritzing sketch freezerbuddy (saved by Fritzing 0.9.10b)
circuit board: 6.1888cm x 5.09679cm
breadboards: 1

parts:
  ARD_NANO = Arduino Nano (Rev3.0)
  DISP = male pin header, 4 pins [form="♂ (male)"]
  TEMP = male pin header, 3 pins [form="♂ (male)"]
  AC_IN = Camdenboss CTB0158-4 [part_number=CTB0158-4 package=THT]
  HLK-PM1 = HLK-PM01
  AQG1 = Panasonic Solid State Relay AQG22205 [mpn=AQG22205 part_number=AQG22205]

nets:
  N1: ARD_NANO.GND, DISP.pin4, TEMP.pin3, HLK-PM1.-Vo, AQG1.-
  N2: ARD_NANO.D2, AQG1.+
  N3: ARD_NANO.D4, DISP.pin1
  N4: ARD_NANO.D5, DISP.pin2
  N5: ARD_NANO.D10, TEMP.pin1
  N6: ARD_NANO.VIN, DISP.pin3, TEMP.pin2, HLK-PM1.+Vo
  N7: AC_IN.pin1, HLK-PM1.AC#1, AQG1.T2
  N8: AC_IN.pin2, AC_IN.pin3, HLK-PM1.AC#0
  N9: AC_IN.pin4, AQG1.T1

notes:
  AC IN
  AC OUT
  +
  -
  D
  freezerbuddy v2
  CLK
  DIO

custom parts:
  Panasonic Solid State Relay AQG22205: Panasonic AQG22205 solid-state relay.
